# Fritzing sketch Robot_V1 (saved by Fritzing 1.0.4)
circuit board: 8.46667cm x 5.64444cm

parts:
  DRV8833_Motor_Driver_Module_1_5A_10V = Adafruit DRV8833 DC/Stepper Motor Driver [part_number=https://www.hestore.hu/prod_10041734.html]
  TT_DC_Motor_3-6V_180mAh = DC Motor [voltage_(max)=6V voltage_(min)=3V]
  TT_DC_Motor_3-6V_180mAh_2 = DC Motor [voltage_(max)=6V voltage_(min)=3V part_number=https://www.hestore.hu/prod_10035529.html]
  HC-SR04_Ultrasonic_Distance_Sensor = HC-SR04 Ultrasonic Distance Sensor [part_number=https://www.hestore.hu/prod_10035534.html]
  ESP32_DEVKIT_V1_350mAh = DOIT Esp32 DevKit v1 (30 pins long, 11 pins width) [part_number=https://www.hestore.hu/prod_10044679.html]
  IP5306/SM5308_based_5V_2A_Step-Up_battery_charging_protection_board = SM5308 battery charger module [part_number=https://www.aliexpress.com/item/1005006255126910.html]
  18650_Li-ion_battery_at_least_1A = Battery Holders [package=lipo-1100mAh]

nets (from the schematic view):
  N1: DRV8833_Motor_Driver_Module_1_5A_10V.PWRIN, IP5306/SM5308_based_5V_2A_Step-Up_battery_charging_protection_board.Pin_1, IP5306/SM5308_based_5V_2A_Step-Up_battery_charging_protection_board.Pin_5, 18650_Li-ion_battery_at_least_1A.+
  GND: DRV8833_Motor_Driver_Module_1_5A_10V.GND, HC-SR04_Ultrasonic_Distance_Sensor.GND, ESP32_DEVKIT_V1_350mAh.GND
  N2: DRV8833_Motor_Driver_Module_1_5A_10V.AOUT2, TT_DC_Motor_3-6V_180mAh.pin_1
  N3: DRV8833_Motor_Driver_Module_1_5A_10V.AOUT1, TT_DC_Motor_3-6V_180mAh.pin_2
  N4: DRV8833_Motor_Driver_Module_1_5A_10V.BOUT1, TT_DC_Motor_3-6V_180mAh_2.pin_1
  N5: DRV8833_Motor_Driver_Module_1_5A_10V.BOUT2, TT_DC_Motor_3-6V_180mAh_2.pin_2
  VCC: DRV8833_Motor_Driver_Module_1_5A_10V.VMOTOR, HC-SR04_Ultrasonic_Distance_Sensor.VCC, ESP32_DEVKIT_V1_350mAh.VIN, IP5306/SM5308_based_5V_2A_Step-Up_battery_charging_protection_board.Pin_4
  N6: DRV8833_Motor_Driver_Module_1_5A_10V.BIN1, ESP32_DEVKIT_V1_350mAh.D23
  N7: DRV8833_Motor_Driver_Module_1_5A_10V.BIN2, ESP32_DEVKIT_V1_350mAh.D22
  N8: DRV8833_Motor_Driver_Module_1_5A_10V.AIN2, ESP32_DEVKIT_V1_350mAh.D21
  N9: DRV8833_Motor_Driver_Module_1_5A_10V.AIN1, ESP32_DEVKIT_V1_350mAh.D19
  N10: HC-SR04_Ultrasonic_Distance_Sensor.TRIG, ESP32_DEVKIT_V1_350mAh.D14
  N11: HC-SR04_Ultrasonic_Distance_Sensor.ECHO, ESP32_DEVKIT_V1_350mAh.D27
  N12: IP5306/SM5308_based_5V_2A_Step-Up_battery_charging_protection_board.Pin_2, 18650_Li-ion_battery_at_least_1A.-

custom parts:
  Adafruit DRV8833 DC/Stepper Motor Driver: Spin two DC motors or step one bi-polar or uni-polar stepper with up to 1.2A per channel using the DRV8833. This motor driver chip is a nice alternative to the TB6612 driver. Like that chip, you get 2 full H-bridges, but this chip is better for low voltage uses (can run from 2.7V up to 10.8V motor power) and has built in current limiting capability. We set it up for 1A current limiting so you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
  DOIT Esp32 DevKit v1 (30 pins long, 11 pins width): The DOIT Esp32 DevKit v1 is one of the development board created by DOIT to evaluate the ESP-WROOM-32 module. It is based on the ESP32 microcontroller that boasts Wifi, Bluetooth, Ethernet and Low Power support all in a single chip. (vanepp) made breadboard work, adjusted pin numbering and labels and reduced size of schematic and cleaned up pcb. This chip is 30pins long (2 x15) and 11 pins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
  SM5308 battery charger module: Charger module for Lipo Battery from Usb, 5v 2a, Sm5308 chip.
