# Fritzing sketch Robot_V2 (saved by Fritzing 1.0.4)

parts:
  DRV8833_Motor_Driver_Module_1_5A_10V = Adafruit DRV8833 DC/Stepper Motor Driver [part_number=https://www.hestore.hu/prod_10041734.html]
  TT_DC_Motor_3-6V_180mAh = DC Motor [voltage_(max)=6V voltage_(min)=3V part_number=https://www.hestore.hu/prod_10035529.html]
  TT_DC_Motor_3-6V_180mAh_2 = DC Motor [voltage_(max)=6V voltage_(min)=3V part_number=https://www.hestore.hu/prod_10035529.html]
  18650_Li-ion_battery_at_least_1A = Battery Holders [package=lipo-1100mAh]
  HC-SR04_Ultrasonic_Distance_Sensor = HC-SR04 Ultrasonic Distance Sensor [part_number=https://www.hestore.hu/prod_10035534.html]
  ESP32_DEVKIT_V1_350mAh = DOIT Esp32 DevKit v1 (30 pins long, 11 pins width) [part_number=https://www.hestore.hu/prod_10044679.html]
  0_9-5V_step-up_600mA_5V = mini boost module [part_number=https://www.hestore.hu/prod_10039261.html]
  TP4056_charge_protection_module = TP4056 [chip_label=TP4056 part_number=https://www.hestore.hu/prod_10042093.html package="DIP (Dual Inline) [THT]"]
  Toggle_switch = Toggle Switch [part_number=https://www.hestore.hu/prod_10022048.html package=THT]

nets:
  N1: DRV8833_Motor_Driver_Module_1_5A_10V.PWRIN, 0_9-5V_step-up_600mA_5V.Pin_2, Toggle_switch.L2
  GND: DRV8833_Motor_Driver_Module_1_5A_10V.GND, HC-SR04_Ultrasonic_Distance_Sensor.GND, ESP32_DEVKIT_V1_350mAh.GND, 0_9-5V_step-up_600mA_5V.Pin_1, 0_9-5V_step-up_600mA_5V.Pin_3, TP4056_charge_protection_module.pin6
  N2: DRV8833_Motor_Driver_Module_1_5A_10V.AOUT2, TT_DC_Motor_3-6V_180mAh.pin_1
  N3: DRV8833_Motor_Driver_Module_1_5A_10V.AOUT1, TT_DC_Motor_3-6V_180mAh.pin_2
  N4: DRV8833_Motor_Driver_Module_1_5A_10V.BOUT1, TT_DC_Motor_3-6V_180mAh_2.pin_1
  N5: DRV8833_Motor_Driver_Module_1_5A_10V.BOUT2, TT_DC_Motor_3-6V_180mAh_2.pin_2
  N6: DRV8833_Motor_Driver_Module_1_5A_10V.BIN1, ESP32_DEVKIT_V1_350mAh.D23
  N7: DRV8833_Motor_Driver_Module_1_5A_10V.BIN2, ESP32_DEVKIT_V1_350mAh.D22
  N8: DRV8833_Motor_Driver_Module_1_5A_10V.AIN2, ESP32_DEVKIT_V1_350mAh.D21
  N9: DRV8833_Motor_Driver_Module_1_5A_10V.AIN1, ESP32_DEVKIT_V1_350mAh.D19
  N10: 18650_Li-ion_battery_at_least_1A.+, TP4056_charge_protection_module.pin4
  N11: 18650_Li-ion_battery_at_least_1A.-, TP4056_charge_protection_module.pin5
  VCC: HC-SR04_Ultrasonic_Distance_Sensor.VCC, ESP32_DEVKIT_V1_350mAh.VIN, 0_9-5V_step-up_600mA_5V.Pin_4
  N12: HC-SR04_Ultrasonic_Distance_Sensor.TRIG, ESP32_DEVKIT_V1_350mAh.D14
  N13: HC-SR04_Ultrasonic_Distance_Sensor.ECHO, ESP32_DEVKIT_V1_350mAh.D27
  N14: TP4056_charge_protection_module.pin3, Toggle_switch.COM

custom parts:
  Adafruit DRV8833 DC/Stepper Motor Driver: Spin two DC motors or step one bi-polar or uni-polar stepper with up to 1.2A per channel using the DRV8833. This motor driver chip is a nice alternative to the TB6612 driver. Like that chip, you get 2 full H-bridges, but this chip is better for low voltage uses (can run from 2.7V up to 10.8V motor power) and has built in current limiting capability. We set it up for 1A current limiting so you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
  DOIT Esp32 DevKit v1 (30 pins long, 11 pins width): The DOIT Esp32 DevKit v1 is one of the development board created by DOIT to evaluate the ESP-WROOM-32 module. It is based on the ESP32 microcontroller that boasts Wifi, Bluetooth, Ethernet and Low Power support all in a single chip. (vanepp) made breadboard work, adjusted pin numbering and labels and reduced size of schematic and cleaned up pcb. This chip is 30pins long (2 x15) and 11 pins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
  mini boost module: mini boost module.
  TP4056: A DIP stand-in part for whatever IC you want. With 6 pins on a 300mil dual inline package (DIP) footprint.
