# Fritzing sketch Robot_V3 (saved by Fritzing 1.0.4)

parts:
  DRV8833_Motor_Driver_Module_1_5A_10_8V = Adafruit DRV8833 DC/Stepper Motor Driver [part_number=https://www.hestore.hu/prod_10041734.html]
  TT_DC_Motor_3-6V_180mAh = DC Motor [voltage_(max)=6V voltage_(min)=3V part_number=https://www.hestore.hu/prod_10035529.html]
  N20_DC_12V_100mA_Brushed_Motor = DC Motor [voltage_(max)=6V voltage_(min)=3V part_number=https://www.hestore.hu/prod_10041795.html]
  HC-SR04_Ultrasonic_Distance_Sensor = HC-SR04 Ultrasonic Distance Sensor [part_number=https://www.hestore.hu/prod_10035534.html]
  ESP32_DEVKIT_V1_350mAh = DOIT Esp32 DevKit v1 (30 pins long, 11 pins width) [part_number=https://www.hestore.hu/prod_10044679.html]
  Toggle_switch = Toggle Switch [part_number=https://www.hestore.hu/prod_10022048.html package=THT]
  10V_2A_DC_input = Power plug
  LM7805_replacement_8-30V_to_5V_1A_voltage_regulator = Voltage Regulator - 5V [part_number=https://www.hestore.hu/prod_10042763.html package="TO220 [THT]"]
  Ceramic_Capacitor = Ceramic Capacitor [capacitance="100 nF" voltage=16V package="0805 [SMD, multilayer]"]  # not connected
  Ceram_Cap = Ceramic Capacitor [capacitance="100 nF" voltage=16V package="0805 [SMD, multilayer]"]  # not connected
  Low_ESR_Electrolit_Capacitor = Electrolytic Capacitor [capacitance=100μF voltage=16V package="0807 [SMD, electrolytic]"]  # not connected

nets:
  N1: DRV8833_Motor_Driver_Module_1_5A_10_8V.PWRIN, Toggle_switch.L2, LM7805_replacement_8-30V_to_5V_1A_voltage_regulator.input_voltage
  GND: DRV8833_Motor_Driver_Module_1_5A_10_8V.GND, HC-SR04_Ultrasonic_Distance_Sensor.GND, ESP32_DEVKIT_V1_350mAh.GND, 10V_2A_DC_input.GND, LM7805_replacement_8-30V_to_5V_1A_voltage_regulator.GND
  N2: DRV8833_Motor_Driver_Module_1_5A_10_8V.AOUT2, TT_DC_Motor_3-6V_180mAh.pin_1
  N3: DRV8833_Motor_Driver_Module_1_5A_10_8V.AOUT1, TT_DC_Motor_3-6V_180mAh.pin_2
  N4: DRV8833_Motor_Driver_Module_1_5A_10_8V.BOUT1, N20_DC_12V_100mA_Brushed_Motor.pin_1
  N5: DRV8833_Motor_Driver_Module_1_5A_10_8V.BOUT2, N20_DC_12V_100mA_Brushed_Motor.pin_2
  N6: DRV8833_Motor_Driver_Module_1_5A_10_8V.BIN1, ESP32_DEVKIT_V1_350mAh.D23
  N7: DRV8833_Motor_Driver_Module_1_5A_10_8V.BIN2, ESP32_DEVKIT_V1_350mAh.D22
  N8: DRV8833_Motor_Driver_Module_1_5A_10_8V.AIN2, ESP32_DEVKIT_V1_350mAh.D21
  N9: DRV8833_Motor_Driver_Module_1_5A_10_8V.AIN1, ESP32_DEVKIT_V1_350mAh.D19
  VCC: HC-SR04_Ultrasonic_Distance_Sensor.VCC, ESP32_DEVKIT_V1_350mAh.VIN, LM7805_replacement_8-30V_to_5V_1A_voltage_regulator.output_voltage
  N10: HC-SR04_Ultrasonic_Distance_Sensor.TRIG, ESP32_DEVKIT_V1_350mAh.D14
  N11: HC-SR04_Ultrasonic_Distance_Sensor.ECHO, ESP32_DEVKIT_V1_350mAh.D27
  N12: Toggle_switch.COM, 10V_2A_DC_input.VCC

custom parts:
  Adafruit DRV8833 DC/Stepper Motor Driver: Spin two DC motors or step one bi-polar or uni-polar stepper with up to 1.2A per channel using the DRV8833. This motor driver chip is a nice alternative to the TB6612 driver. Like that chip, you get 2 full H-bridges, but this chip is better for low voltage uses (can run from 2.7V up to 10.8V motor power) and has built in current limiting capability. We set it up for 1A current limiting so you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
  DOIT Esp32 DevKit v1 (30 pins long, 11 pins width): The DOIT Esp32 DevKit v1 is one of the development board created by DOIT to evaluate the ESP-WROOM-32 module. It is based on the ESP32 microcontroller that boasts Wifi, Bluetooth, Ethernet and Low Power support all in a single chip. (vanepp) made breadboard work, adjusted pin numbering and labels and reduced size of schematic and cleaned up pcb. This chip is 30pins long (2 x15) and 11 pins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
